// Logisim project UAL.circ as structural Verilog: 5 circuits, main circuit main
module main (
  input  Chiffre_1,
  input  in_2,
  input  in_3,
  input  in_4,
  input  Chiffre_2,
  input  in_6,
  input  in_7,
  input  in_8,
  input  [2:0] in_9,
  output Bit_0,
  output Bit_1,
  output Bit_2,
  output Bit_3,
  output out_14
);

  wire ADD0, ADD1, ADD2, ADD3, CO0, CO1, CO2, CO3, CO20, CO21, CO22, CO23, ET0, ET1, ET2, ET3, OU0, OU1, OU2,
       OU3, RETENUE, RETENUE2;

  Additionneur additionneur_1 (
    .Bit_0(in_4), .Bit_0_2(in_8), .in_3(1'b0), .Bit_1(in_3), .Bit_1_2(in_7), .Bit_2(in_2), .Bit_2_2(in_6),
    .Bit_3(Chiffre_1), .Bit_3_2(Chiffre_2), .out_10(ADD0), .out_11(ADD1), .out_12(ADD2), .out_13(ADD3),
    .out_14(RETENUE));
  \Complément  \complément_1  (
    .in_1(ADD0), .in_2(ADD1), .in_3(ADD2), .in_4(ADD3), .out_5(CO0), .out_6(CO1), .out_7(CO2), .out_8(CO3));
  ET_logique et_logique_1 (
    .in_1(in_4), .in_2(in_8), .in_3(in_3), .in_4(in_7), .in_5(in_2), .in_6(in_6), .in_7(Chiffre_1),
    .in_8(Chiffre_2), .out_9(ET0), .out_10(ET1), .out_11(ET2), .out_12(ET3));
  OU_logique ou_logique_1 (
    .in_1(in_4), .in_2(in_8), .in_3(in_3), .in_4(in_7), .in_5(in_2), .in_6(in_6), .in_7(Chiffre_1),
    .in_8(Chiffre_2), .out_9(OU0), .out_10(OU1), .out_11(OU2), .out_12(OU3));
  Additionneur additionneur_2 (
    .Bit_0(CO0), .Bit_0_2(1'b1), .in_3(1'b0), .Bit_1(CO1), .Bit_1_2(1'b0), .Bit_2(CO2), .Bit_2_2(1'b0),
    .Bit_3(CO3), .Bit_3_2(1'b0), .out_10(CO20), .out_11(CO21), .out_12(CO22), .out_13(CO23), .out_14(RETENUE2));
  Multiplexer #(.select(3)) multiplexer_1 (
    .in0(ADD0), .in1(CO0), .in2(ET0), .in3(OU0), .in4(CO20), .out(Bit_0), .sel(in_9));  // open: in5, in6, in7, en
  Multiplexer #(.select(3)) multiplexer_2 (
    .in0(ADD1), .in1(CO1), .in2(ET1), .in3(OU1), .in4(CO21), .out(Bit_1), .sel(in_9));  // open: in5, in6, in7, en
  Multiplexer #(.select(3)) multiplexer_3 (
    .in0(ADD2), .in1(CO2), .in2(ET2), .in3(OU2), .in4(CO22), .out(Bit_2), .sel(in_9));  // open: in5, in6, in7, en
  Multiplexer #(.select(3)) multiplexer_4 (
    .in0(ADD3), .in1(CO3), .in2(ET3), .in3(OU3), .in4(CO23), .out(Bit_3), .sel(in_9));  // open: in5, in6, in7, en
  Multiplexer #(.select(3)) multiplexer_5 (
    .in0(RETENUE), .in4(RETENUE2), .out(out_14), .sel(in_9));  // open: in1, in2, in3, in5, in6, in7, en

  // Notes on the sheet:
  //   Retenue à 0
  //   Additionneur
  //   Complément à 1
  //   ET
  //   OU
  //   Complément à 2
  //   000 = Addition
  //   001 = Complément à 1
  //   010 = ET Logique
  //   011 = OU Logique
  //   100 = Complément à 2
  //   RESULTAT
  //   Bit 4 (débordement)
endmodule

module Additionneur (
  input  Bit_0,
  input  Bit_0_2,
  input  in_3,
  input  Bit_1,
  input  Bit_1_2,
  input  Bit_2,
  input  Bit_2_2,
  input  Bit_3,
  input  Bit_3_2,
  output out_10,
  output out_11,
  output out_12,
  output out_13,
  output out_14
);

  wire and_1_out, and_2_out, and_3_out, and_4_out, and_5_out, and_6_out, and_7_out, and_8_out, Retenue0,
       Retenue1, Retenue2, xor_1_out, xor_2_out, xor_3_out, xor_4_out;

  xor xor_1 (xor_1_out, Bit_0, Bit_0_2);
  and and_1 (and_1_out, Bit_0, Bit_0_2);
  xor xor_2 (xor_2_out, Bit_1, Bit_1_2);
  and and_2 (and_2_out, Bit_1, Bit_1_2);
  xor xor_3 (xor_3_out, Bit_2, Bit_2_2);
  and and_3 (and_3_out, Bit_2, Bit_2_2);
  xor xor_4 (xor_4_out, Bit_3, Bit_3_2);
  and and_4 (and_4_out, Bit_3, Bit_3_2);
  and and_5 (and_5_out, xor_1_out, in_3);
  and and_6 (and_6_out, xor_2_out, Retenue0);
  and and_7 (and_7_out, xor_3_out, Retenue1);
  and and_8 (and_8_out, xor_4_out, Retenue2);
  xor xor_5 (out_10, xor_1_out, in_3);
  xor xor_6 (out_11, xor_2_out, Retenue0);
  xor xor_7 (out_12, xor_3_out, Retenue1);
  xor xor_8 (out_13, xor_4_out, Retenue2);
  or or_1 (Retenue0, and_5_out, and_1_out);
  or or_2 (Retenue1, and_6_out, and_2_out);
  or or_3 (Retenue2, and_7_out, and_3_out);
  or or_4 (out_14, and_8_out, and_4_out);

  // Notes on the sheet:
  //   Chiffre 1 
  //   Chiffre 2
  //   Chiffre 1 
  //   Chiffre 2
  //   Chiffre 1 
  //   Chiffre 2
  //   Chiffre 1 
  //   Chiffre 2
endmodule

module \Complément  (
  input  in_1,
  input  in_2,
  input  in_3,
  input  in_4,
  output out_5,
  output out_6,
  output out_7,
  output out_8
);

  not not_1 (out_5, in_1);
  not not_2 (out_6, in_2);
  not not_3 (out_7, in_3);
  not not_4 (out_8, in_4);
endmodule

module ET_logique (
  input  in_1,
  input  in_2,
  input  in_3,
  input  in_4,
  input  in_5,
  input  in_6,
  input  in_7,
  input  in_8,
  output out_9,
  output out_10,
  output out_11,
  output out_12
);

  and and_1 (out_9, in_1, in_2);
  and and_2 (out_10, in_3, in_4);
  and and_3 (out_11, in_5, in_6);
  and and_4 (out_12, in_7, in_8);
endmodule

module OU_logique (
  input  in_1,
  input  in_2,
  input  in_3,
  input  in_4,
  input  in_5,
  input  in_6,
  input  in_7,
  input  in_8,
  output out_9,
  output out_10,
  output out_11,
  output out_12
);

  or or_1 (out_9, in_1, in_2);
  or or_2 (out_10, in_3, in_4);
  or or_3 (out_11, in_5, in_6);
  or or_4 (out_12, in_7, in_8);
endmodule
